// Logisim project piped.circ as structural Verilog: 6 circuits, main circuit main
module main (
);

  wire Clock, ex_mem_1_zero_read, mips_alu_1_p3, registerfile_1_p2;
  wire [4:0] instructiondecode_1__16_20, instructiondecode_1__21_25;
  wire [15:0] instructiondecode_1__0_15;
  wire [31:0] adder_1_out, adder_2_out, bit_extender_1_out, ex_mem_1_branch_address_read, ex_mem_1_out_9,
       ex_mem_1_register_read_data_2_read, id_ex_1_immediate_field_write_2, id_ex_1_incremented_pc_read,
       id_ex_1_register_read_data_1_write_2, id_ex_1_register_read_data_2_read, if_id_1_out_4, if_id_1_out_5,
       mem_wb_1_alu_result_read, mem_wb_1_read_data_write_2, mips_alu_1_p2, mips_alu_1_p4, mips_ram_1_p5,
       mipsprogramrom_1_p2, mipsprogramrom_1_p3, multiplexer_1_out, PC_q, registerfile_1_p6,
       registerfile_1_p7, shifter_1_out;

  Clock clock_1 (.out(Clock));
  Register #(.width(32)) PC (.D(multiplexer_1_out), .Q(PC_q), .clk(Clock));  // open: en, clr
  Multiplexer #(.width(32), .enable("false")) multiplexer_1 (
    .in0(adder_1_out), .in1(ex_mem_1_branch_address_read), .out(multiplexer_1_out));  // open: sel
  Adder #(.width(32)) adder_1 (.a(PC_q), .b(32'h4), .out(adder_1_out));  // open: cin, cout
  // MIPSProgramROM mipsprogramrom_1: pin names not known; wires that end beside it: PC_q, mipsprogramrom_1_p2, mipsprogramrom_1_p3
  IF_ID if_id_1 (
    .in_1(adder_1_out), .in_2(mipsprogramrom_1_p2), .out_4(if_id_1_out_4), .out_5(if_id_1_out_5),
    .Clock(Clock));
  instructionDecode instructiondecode_1 (
    ._32_bit_instruction(if_id_1_out_5), ._21_25(instructiondecode_1__21_25),
    ._16_20(instructiondecode_1__16_20), ._0_15(instructiondecode_1__0_15));  // open: _26_31, _11_15, _0_5
  // RegisterFile registerfile_1: pin names not known; wires that end beside it: Clock, registerfile_1_p2, registerfile_1_p2, instructiondecode_1__21_25, instructiondecode_1__16_20, registerfile_1_p6, registerfile_1_p7
  assign bit_extender_1_out = {{16{instructiondecode_1__0_15[15]}}, instructiondecode_1__0_15};  // Bit_Extender bit_extender_1
  ID_EX id_ex_1 (
    .Incremented_PC_write(if_id_1_out_4), .Register_read_data_1_write(registerfile_1_p6),
    .Register_read_data_2_write(registerfile_1_p7), .Immediate_field_write(bit_extender_1_out),
    .Clock(Clock), .Incremented_PC_read(id_ex_1_incremented_pc_read),
    .Register_read_data_1_write_2(id_ex_1_register_read_data_1_write_2),
    .Register_read_data_2_read(id_ex_1_register_read_data_2_read),
    .Immediate_field_write_2(id_ex_1_immediate_field_write_2));
  Shifter #(.width(32)) shifter_1 (.in(id_ex_1_immediate_field_write_2), .\dist (5'b00010), .out(shifter_1_out));
  // MIPS_ALU mips_alu_1: pin names not known; wires that end beside it: id_ex_1_register_read_data_1_write_2, mips_alu_1_p2, mips_alu_1_p3, mips_alu_1_p4
  Multiplexer #(.width(32), .enable("false")) multiplexer_2 (
    .in0(id_ex_1_register_read_data_2_read), .in1(id_ex_1_immediate_field_write_2), .out(mips_alu_1_p2));  // open: sel
  Adder #(.width(32)) adder_2 (
    .a(id_ex_1_incremented_pc_read), .b(shifter_1_out), .out(adder_2_out));  // open: cin, cout
  EX_MEM ex_mem_1 (
    .Branch_address_write(adder_2_out), .Zero_write(mips_alu_1_p3),
    .Register_read_data_2_write(mips_alu_1_p4), .in_4(id_ex_1_register_read_data_2_read), .Clock(Clock),
    .Branch_address_read(ex_mem_1_branch_address_read), .Zero_read(ex_mem_1_zero_read),
    .Register_read_data_2_read(ex_mem_1_register_read_data_2_read), .out_9(ex_mem_1_out_9));
  // MIPS_RAM mips_ram_1: pin names not known; wires that end beside it: ex_mem_1_zero_read, ex_mem_1_register_read_data_2_read, ex_mem_1_out_9, Clock, mips_ram_1_p5
  MEM_WB mem_wb_1 (
    .Read_data_write(mips_ram_1_p5), .ALU_result_write(ex_mem_1_register_read_data_2_read), .Clock(Clock),
    .Read_data_write_2(mem_wb_1_read_data_write_2), .ALU_result_read(mem_wb_1_alu_result_read));
  Multiplexer #(.width(32), .enable("false")) multiplexer_3 (
    .in0(mem_wb_1_read_data_write_2), .in1(mem_wb_1_alu_result_read), .out(mipsprogramrom_1_p3));  // open: sel
endmodule

module IF_ID (
  input  [31:0] in_1,
  input  [31:0] in_2,
  input  Clock,
  output [31:0] out_4,
  output [31:0] out_5
);

  Register #(.width(32)) Incremented_PC (.D(in_1), .Q(out_4), .clk(Clock));  // open: en, clr
  Register #(.width(32)) Fetched_instruction (.D(in_2), .Q(out_5), .clk(Clock));  // open: en, clr
endmodule

module ID_EX (
  input  [31:0] Incremented_PC_write,
  input  [31:0] Register_read_data_1_write,
  input  [31:0] Register_read_data_2_write,
  input  [31:0] Immediate_field_write,
  input  Clock,
  output [31:0] Incremented_PC_read,
  output [31:0] Register_read_data_1_write_2,
  output [31:0] Register_read_data_2_read,
  output [31:0] Immediate_field_write_2
);

  Register #(.width(32)) Incremented_PC (
    .D(Incremented_PC_write), .Q(Incremented_PC_read), .clk(Clock));  // open: en, clr
  Register #(.width(32)) Register_read_data_1 (
    .D(Register_read_data_1_write), .Q(Register_read_data_1_write_2), .clk(Clock));  // open: en, clr
  Register #(.width(32)) Register_read_data_2 (
    .D(Register_read_data_2_write), .Q(Register_read_data_2_read), .clk(Clock));  // open: en, clr
  Register #(.width(32)) Immediate_field (
    .D(Immediate_field_write), .Q(Immediate_field_write_2), .clk(Clock));  // open: en, clr
endmodule

module instructionDecode (
  input  [31:0] _32_bit_instruction,
  output [5:0] _26_31,
  output [4:0] _21_25,
  output [4:0] _16_20,
  output [15:0] _0_15,
  output [4:0] _11_15,
  output [5:0] _0_5
);


  assign _0_5 = _32_bit_instruction[5:0];
  assign _0_15 = _32_bit_instruction[15:0];
  assign _11_15 = _32_bit_instruction[15:11];
  assign _16_20 = _32_bit_instruction[20:16];
  assign _21_25 = _32_bit_instruction[25:21];
  assign _26_31 = _32_bit_instruction[31:26];
endmodule

module EX_MEM (
  input  [31:0] Branch_address_write,
  input  Zero_write,
  input  [31:0] Register_read_data_2_write,
  input  [31:0] in_4,
  input  Clock,
  output [31:0] Branch_address_read,
  output Zero_read,
  output [31:0] Register_read_data_2_read,
  output [31:0] out_9
);

  Register #(.width(32)) Branch_address (
    .D(Branch_address_write), .Q(Branch_address_read), .clk(Clock));  // open: en, clr
  Register #(.width(1)) Zero (.D(Zero_write), .Q(Zero_read), .clk(Clock));  // open: en, clr
  Register #(.width(32)) Register_read_data_2 (
    .D(Register_read_data_2_write), .Q(Register_read_data_2_read), .clk(Clock));  // open: en, clr
  Register #(.width(32)) register_1 (.D(in_4), .Q(out_9), .clk(Clock));  // open: en, clr
endmodule

module MEM_WB (
  input  [31:0] Read_data_write,
  input  [31:0] ALU_result_write,
  input  Clock,
  output [31:0] Read_data_write_2,
  output [31:0] ALU_result_read
);

  Register #(.width(32)) Read_data (.D(Read_data_write), .Q(Read_data_write_2), .clk(Clock));  // open: en, clr
  Register #(.width(32)) ALU_result (.D(ALU_result_write), .Q(ALU_result_read), .clk(Clock));  // open: en, clr
endmodule
